# Fritzing sketch Skema TA 2 (saved by Fritzing 0.9.5d)
breadboards: 1

parts:
  DHT1 = DHT11 Humitidy and Temperature Sensor (3 pins)
  M1 = DOIT Esp32 DevKit v1 (30 pins long, 11 pins width) [part_number=ESP32S-PIN30]  # not connected
  Part1 = HY-SRF05 Ultrasonic Rangefinder
  J1 = Basic Servo
  M2 = fc-51 [package=THT]
  J2 = Piezo Speaker
  A1 = DORHEA ESP32 GPIO breakout board 30pin

nets:
  N1: DHT1.Plus, A1.Pin_70, A1.Pin_117
  N2: DHT1.Signal, M2.pin3, A1.Pin_14, A1.Pin_21, A1.Pin_64, A1.Pin_104
  GND: DHT1.Gnd, Part1.GND, J1.gnd, M2.pin2, J2.pin1, A1.Pin_27, A1.Pin_34, A1.Pin_55, A1.Pin_56, A1.Pin_58, A1.Pin_67, A1.Pin_91
  VCC: Part1.Vcc, J1.vcc, A1.Pin_59, A1.Pin_60, A1.Pin_63
  N3: Part1.Trig, A1.Pin_80, A1.Pin_127
  N4: Part1.Echo, A1.Pin_79, A1.Pin_126
  N5: J1.pulse, A1.Pin_116
  N6: M2.pin1, A1.Pin_8
  N7: J2.pin2, A1.Pin_13, A1.Pin_52

notes:
  (5) Sensor Suhu dan Kelembaban
  (4) Sensor Ultrasonik/Jarak
  (6) Sensor Infrared
  (3) Motor Servo
  (1) NodeMCU ESP32
  (2) Expansion Board ESP32
  (7) Buzzer

custom parts:
  DHT11 Humitidy and Temperature Sensor (3 pins): DHT11 Humidity and Temperature Sensor (3 pins).
  DOIT Esp32 DevKit v1 (30 pins long, 11 pins width): The DOIT Esp32 DevKit v1 is one of the development board created by DOIT to evaluate the ESP-WROOM-32 module. It is based on the ESP32 microcontroller that boasts Wifi, Bluetooth, Ethernet and Low Power support all in a single chip. (vanepp) made breadboard work, adjusted pin numbering and labels and reduced size of schematic and cleaned up pcb. This chip is 30pins long (2 x15) and 11 pins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
  DORHEA ESP32 GPIO breakout board 30pin: ESP32 shield 30P expansion board, supports two power supply : DC 6.5-16v and USB 5.V
